# Fritzing sketch IMU_Sketch (saved by Fritzing 0.9.3b)
circuit board: 4.00669cm x 4.47993cm
breadboards: 1

parts:
  Arduino = Arduino Nano (Rev3.0) (ICSP)
  IMU = GY-5150 (MPU-9150) [form="♀ (female)" package=THT]

nets:
  N1: Arduino.GND, IMU.pin2
  N2: Arduino.5V, IMU.pin1
  N3: Arduino.A5, IMU.pin3
  N4: Arduino.A4, IMU.pin4

custom parts:
  GY-5150 (MPU-9150): Placa GY-5150 basada en conjunto de acelerómetro+giroscopios+magnetómetro MPU-9150
